# Fritzing sketch zad2 (saved by Fritzing 0.9.3b)
breadboards: 1

parts:
  Part1 = Arduino Uno (Rev3)
  R1 = Resistor [tolerance=±5% resistance=220 package=THT]
  R2 = Photocell (LDR) [package=THT]
  R3 = Resistor [tolerance=±5% resistance=220 package=THT]
  LED1 = LED - 5mm [color="Red (633nm)" package="5 mm [THT]"]
  R4 = Resistor [tolerance=±5% resistance=1k package=THT]
  R5 = Resistor [tolerance=±5% resistance=1k package=THT]
  Maximum_button = Pushbutton [package="[THT]"]
  Minimum_button = Pushbutton [package="[THT]"]

nets:
  N1: Part1.A0, R1.Pin_1, R2.pin_0
  N2: Part1.D9_PWM, LED1.anode
  N3: Part1.D2, R5.Pin_0, Maximum_button.Pin_3, Maximum_button.Pin_4
  N4: Part1.D3_PWM, R4.Pin_0, Minimum_button.Pin_3, Minimum_button.Pin_4
  N5: Part1.5V, R2.pin_1, Maximum_button.Pin_1, Maximum_button.Pin_2, Minimum_button.Pin_1, Minimum_button.Pin_2
  N6: Part1.GND, R1.Pin_0, R3.Pin_1, R4.Pin_1, R5.Pin_1
  N7: R3.Pin_0, LED1.cathode

notes:
  Fioletowy kabel - max
  Niebieski kabel - min
