# Fritzing sketch zad4 (saved by Fritzing 0.9.3b)
breadboards: 1

parts:
  S1 = Pushbutton [package="[THT]"]
  R3 = Resistor [tolerance=±5% resistance=220 package=THT]
  J1 = Piezo Speaker
  LED1 = LED - 5mm [color="Red (633nm)" package="5 mm [THT]"]
  R4 = Resistor [tolerance=±5% resistance=220 package=THT]
  Part2 = Arduino Motor Shield (Rev3)

nets:
  N1: S1.Pin_1, S1.Pin_2, Part2.5V
  N2: S1.Pin_3, S1.Pin_4, R3.Pin_1, Part2.D13/DirB
  N3: R3.Pin_0, J1.pin1, R4.Pin_1, Part2.GND
  N4: J1.pin2, Part2.D2
  N5: LED1.cathode, Part2.D10_PWM
  N6: LED1.anode, R4.Pin_0

notes:
  Podłączamy TinkerKit do Arduino, a następnie kabelki do TinkerKita w sposób jak na obrazku. Następnie detektor elektromagnetyczny podłączamy pod In0.
